// Logisim project somador.circ as structural Verilog: 4 circuits, main circuit Meio Somador
module Meio_Somador (
  input  A0,
  input  B0,
  output S0,
  output Co0
);

  xor xor_1 (S0, A0, B0);
  and and_1 (Co0, A0, B0);

  // Notes on the sheet:
  //   Meio somador
endmodule

module Somador_Completo (
  input  A0,
  input  B0,
  input  Ci0,
  output S0,
  output Co0
);

  wire meio_somador_1_co0, meio_somador_1_s0, meio_somador_2_co0;

  Meio_Somador meio_somador_1 (.A0(A0), .B0(B0), .S0(meio_somador_1_s0), .Co0(meio_somador_1_co0));
  Meio_Somador meio_somador_2 (.A0(meio_somador_1_s0), .B0(Ci0), .S0(S0), .Co0(meio_somador_2_co0));
  or or_1 (Co0, meio_somador_2_co0, meio_somador_1_co0);

  // Notes on the sheet:
  //   Somador Completo
endmodule

module Somador_de_4_bits (
  input  [3:0] A,
  input  Carry_in,
  input  [3:0] B,
  output [3:0] S,
  output Over_flow,
  output Carry_out
);

  wire somador_completo_1_co0, somador_completo_2_co0, somador_completo_3_co0;

  Somador_Completo somador_completo_1 (.A0(A[0]), .B0(B[0]), .Ci0(Carry_in), .S0(S[0]), .Co0(somador_completo_1_co0));
  Somador_Completo somador_completo_2 (
    .A0(A[1]), .B0(B[1]), .Ci0(somador_completo_1_co0), .S0(S[1]), .Co0(somador_completo_2_co0));
  Somador_Completo somador_completo_3 (
    .A0(A[2]), .B0(B[2]), .Ci0(somador_completo_2_co0), .S0(S[2]), .Co0(somador_completo_3_co0));
  Somador_Completo somador_completo_4 (.A0(A[3]), .B0(B[3]), .Ci0(somador_completo_3_co0), .S0(S[3]), .Co0(Carry_out));
  xor xor_1 (Over_flow, somador_completo_3_co0, Carry_out);

  // Notes on the sheet:
  //   +
endmodule

module main (
  input  Carry_In,
  input  [3:0] A,
  input  [3:0] B,
  output [3:0] S,
  output Carry_Out,
  output Over_Flow
);

  wire displaydecoder_1_p2, displaydecoder_1_p3, displaydecoder_1_p4, displaydecoder_1_p5,
       displaydecoder_1_p6, displaydecoder_1_p7, displaydecoder_1_p8, displaydecoder_2_p2,
       displaydecoder_2_p3, displaydecoder_2_p4, displaydecoder_2_p5, displaydecoder_2_p6,
       displaydecoder_2_p7, displaydecoder_2_p8, displaydecoder_3_p2, displaydecoder_3_p3,
       displaydecoder_3_p4, displaydecoder_3_p5, displaydecoder_3_p6, displaydecoder_3_p7,
       displaydecoder_3_p8;

  // DisplayDecoder displaydecoder_1: pin names not known; wires that end beside it: A, displaydecoder_1_p2, displaydecoder_1_p3, displaydecoder_1_p4, displaydecoder_1_p5, displaydecoder_1_p6, displaydecoder_1_p7, displaydecoder_1_p8
  Somador_de_4_bits somador_de_4_bits_1 (
    .A(A), .B(B), .Carry_in(Carry_In), .Carry_out(Carry_Out), .S(S), .Over_flow(Over_Flow));
  // DisplayDecoder displaydecoder_2: pin names not known; wires that end beside it: B, displaydecoder_2_p2, displaydecoder_2_p3, displaydecoder_2_p4, displaydecoder_2_p5, displaydecoder_2_p6, displaydecoder_2_p7, displaydecoder_2_p8
  _7_Segment_Display u_7_segment_display_1 (
    .g(displaydecoder_1_p8), .f(displaydecoder_1_p7), .a(displaydecoder_1_p2), .b(displaydecoder_1_p3),
    .e(displaydecoder_1_p6), .d(displaydecoder_1_p5), .c(displaydecoder_1_p4));  // open: dp
  _7_Segment_Display u_7_segment_display_2 (
    .g(displaydecoder_2_p8), .f(displaydecoder_2_p7), .a(displaydecoder_2_p2), .b(displaydecoder_2_p3),
    .e(displaydecoder_2_p6), .d(displaydecoder_2_p5), .c(displaydecoder_2_p4));  // open: dp
  // DisplayDecoder displaydecoder_3: pin names not known; wires that end beside it: S, displaydecoder_3_p2, displaydecoder_3_p3, displaydecoder_3_p4, displaydecoder_3_p5, displaydecoder_3_p6, displaydecoder_3_p7, displaydecoder_3_p8
  _7_Segment_Display u_7_segment_display_3 (
    .g(displaydecoder_3_p8), .f(displaydecoder_3_p7), .a(displaydecoder_3_p2), .b(displaydecoder_3_p3),
    .e(displaydecoder_3_p6), .d(displaydecoder_3_p5), .c(displaydecoder_3_p4));  // open: dp

  // Notes on the sheet:
  //   Calculadora de 4 bits
  //   +
endmodule
